// Digital circuit register-file.dig as structural Verilog
module register_file (
  input  [31:0] ReadReg1,
  input  [31:0] ReadReg2,
  input  [4:0] WriteReg,
  input  [31:0] WriteData,
  input  RegWrite,
  input  Clock,
  output [31:0] ReadData1,
  output [31:0] ReadData2
);

  wire and_1_out, and_2_out, and_3_out, and_4_out, and_5_out, and_6_out, and_7_out, and_8_out, and_9_out,
       and_10_out, and_11_out, and_12_out, and_13_out, and_14_out, and_15_out, and_16_out, and_17_out,
       and_18_out, and_19_out, and_20_out, and_21_out, and_22_out, and_23_out, and_24_out, and_25_out,
       and_26_out, and_27_out, and_28_out, and_29_out, and_30_out, and_31_out, Y0, Y1, Y2, Y3, Y4, Y5, Y6,
       Y7, Y8, Y9, Y10, Y11, Y12, Y13, Y14, Y15, Y16, Y17, Y18, Y19, Y20, Y21, Y22, Y23, Y24, Y25, Y26, Y27,
       Y28, Y29, Y30, Y31;
  wire [31:0] R0, R1, R2, R3, R4, R5, R6, R7, R8, R9, R10, R11, R12, R13, R14, R15, R16, R17, R18, R19, R20,
       R21, R22, R23, R24, R25, R26, R27, R28, R29, R30, R31;

  Multiplexer #(.Selector_Bits(5), .Bits(32)) multiplexer_1 (
    .sel(ReadData2[4:0]), .in_0(R31), .in_1(R30), .in_2(R29), .in_3(R28), .in_4(R27), .in_5(R26), .in_6(R25),
    .in_7(R24), .in_8(R23), .in_9(R22), .in_10(R21), .in_11(R20), .in_12(R19), .in_13(R18), .in_14(R17),
    .in_15(R16), .in_16(R15), .in_17(R14), .in_18(R13), .in_19(R12), .in_20(R11), .in_21(R10), .in_22(R9),
    .in_23(R8), .in_24(R7), .in_25(R6), .in_26(R5), .in_27(R4), .in_28(R3), .in_29(R2), .in_30(R1),
    .in_31(R0), .out(ReadReg2));
  and and_1 (and_1_out, Y1, RegWrite);
  and and_2 (and_2_out, Y2, RegWrite);
  and and_3 (and_3_out, Y3, RegWrite);
  and and_4 (and_4_out, Y4, RegWrite);
  and and_5 (and_5_out, Y5, RegWrite);
  and and_6 (and_6_out, Y6, RegWrite);
  and and_7 (and_7_out, Y7, RegWrite);
  Register #(.Bits(32)) reg0 (.D(WriteData), .C(Clock), .en(1'b0), .Q(R0));
  Register #(.Bits(32)) reg1 (.D(WriteData), .C(Clock), .en(and_1_out), .Q(R1));
  Register #(.Bits(32)) reg2 (.D(WriteData), .C(Clock), .en(and_2_out), .Q(R2));
  Register #(.Bits(32)) reg3 (.D(WriteData), .C(Clock), .en(and_3_out), .Q(R3));
  Register #(.Bits(32)) reg4 (.D(WriteData), .C(Clock), .en(and_4_out), .Q(R4));
  Register #(.Bits(32)) reg5 (.D(WriteData), .C(Clock), .en(and_5_out), .Q(R5));
  Register #(.Bits(32)) reg6 (.D(WriteData), .C(Clock), .en(and_6_out), .Q(R6));
  Register #(.Bits(32)) reg7 (.D(WriteData), .C(Clock), .en(and_7_out), .Q(R7));
  and and_8 (and_8_out, Y8, RegWrite);
  and and_9 (and_9_out, Y9, RegWrite);
  and and_10 (and_10_out, Y10, RegWrite);
  and and_11 (and_11_out, Y11, RegWrite);
  and and_12 (and_12_out, Y12, RegWrite);
  and and_13 (and_13_out, Y13, RegWrite);
  and and_14 (and_14_out, Y14, RegWrite);
  and and_15 (and_15_out, Y15, RegWrite);
  Multiplexer #(.Bits(32), .Selector_Bits(5)) multiplexer_2 (
    .sel(ReadData1[4:0]), .in_0(R31), .in_1(R30), .in_2(R29), .in_3(R28), .in_4(R27), .in_5(R26), .in_6(R25),
    .in_7(R24), .in_8(R23), .in_9(R22), .in_10(R21), .in_11(R20), .in_12(R19), .in_13(R18), .in_14(R17),
    .in_15(R16), .in_16(R15), .in_17(R14), .in_18(R13), .in_19(R12), .in_20(R11), .in_21(R10), .in_22(R9),
    .in_23(R8), .in_24(R7), .in_25(R6), .in_26(R5), .in_27(R4), .in_28(R3), .in_29(R2), .in_30(R1),
    .in_31(R0), .out(ReadReg1));
  Register #(.Bits(32)) reg8 (.D(WriteData), .C(Clock), .en(and_8_out), .Q(R8));
  Register #(.Bits(32)) reg9 (.D(WriteData), .C(Clock), .en(and_9_out), .Q(R9));
  Register #(.Bits(32)) reg10 (.D(WriteData), .C(Clock), .en(and_10_out), .Q(R10));
  Register #(.Bits(32)) reg11 (.D(WriteData), .C(Clock), .en(and_11_out), .Q(R11));
  Register #(.Bits(32)) reg12 (.D(WriteData), .C(Clock), .en(and_12_out), .Q(R12));
  Register #(.Bits(32)) reg13 (.D(WriteData), .C(Clock), .en(and_13_out), .Q(R13));
  Register #(.Bits(32)) reg14 (.D(WriteData), .C(Clock), .en(and_14_out), .Q(R14));
  Register #(.Bits(32)) reg15 (.D(WriteData), .C(Clock), .en(and_15_out), .Q(R15));
  and and_16 (and_16_out, Y16, RegWrite);
  and and_17 (and_17_out, Y17, RegWrite);
  and and_18 (and_18_out, Y18, RegWrite);
  and and_19 (and_19_out, Y19, RegWrite);
  and and_20 (and_20_out, Y20, RegWrite);
  and and_21 (and_21_out, Y21, RegWrite);
  and and_22 (and_22_out, Y22, RegWrite);
  and and_23 (and_23_out, Y23, RegWrite);
  Decoder #(.Selector_Bits(5)) decoder_1 (
    .sel(WriteReg), .out_0(Y0), .out_1(Y1), .out_2(Y2), .out_3(Y3), .out_4(Y4), .out_5(Y5), .out_6(Y6),
    .out_7(Y7), .out_8(Y8), .out_9(Y9), .out_10(Y10), .out_11(Y11), .out_12(Y12), .out_13(Y13), .out_14(Y14),
    .out_15(Y15), .out_16(Y16), .out_17(Y17), .out_18(Y18), .out_19(Y19), .out_20(Y20), .out_21(Y21),
    .out_22(Y22), .out_23(Y23), .out_24(Y24), .out_25(Y25), .out_26(Y26), .out_27(Y27), .out_28(Y28),
    .out_29(Y29), .out_30(Y30), .out_31(Y31));
  Register #(.Bits(32)) reg16 (.D(WriteData), .C(Clock), .en(and_16_out), .Q(R16));
  Register #(.Bits(32)) reg17 (.D(WriteData), .C(Clock), .en(and_17_out), .Q(R17));
  Register #(.Bits(32)) reg18 (.D(WriteData), .C(Clock), .en(and_18_out), .Q(R18));
  Register #(.Bits(32)) reg19 (.D(WriteData), .C(Clock), .en(and_19_out), .Q(R19));
  Register #(.Bits(32)) reg20 (.D(WriteData), .C(Clock), .en(and_20_out), .Q(R20));
  Register #(.Bits(32)) reg21 (.D(WriteData), .C(Clock), .en(and_21_out), .Q(R21));
  Register #(.Bits(32)) reg22 (.D(WriteData), .C(Clock), .en(and_22_out), .Q(R22));
  Register #(.Bits(32)) reg23 (.D(WriteData), .C(Clock), .en(and_23_out), .Q(R23));
  and and_24 (and_24_out, Y24, RegWrite);
  and and_25 (and_25_out, Y25, RegWrite);
  and and_26 (and_26_out, Y26, RegWrite);
  and and_27 (and_27_out, Y27, RegWrite);
  and and_28 (and_28_out, Y28, RegWrite);
  and and_29 (and_29_out, Y29, RegWrite);
  and and_30 (and_30_out, Y30, RegWrite);
  and and_31 (and_31_out, Y31, RegWrite);
  Register #(.Bits(32)) reg24 (.D(WriteData), .C(Clock), .en(and_24_out), .Q(R24));
  Register #(.Bits(32)) reg25 (.D(WriteData), .C(Clock), .en(and_25_out), .Q(R25));
  Register #(.Bits(32)) reg26 (.D(WriteData), .C(Clock), .en(and_26_out), .Q(R26));
  Register #(.Bits(32)) reg27 (.D(WriteData), .C(Clock), .en(and_27_out), .Q(R27));
  Register #(.Bits(32)) reg28 (.D(WriteData), .C(Clock), .en(and_28_out), .Q(R28));
  Register #(.Bits(32)) reg29 (.D(WriteData), .C(Clock), .en(and_29_out), .Q(R29));
  Register #(.Bits(32)) reg30 (.D(WriteData), .C(Clock), .en(and_30_out), .Q(R30));
  Register #(.Bits(32)) reg31 (.D(WriteData), .C(Clock), .en(and_31_out), .Q(R31));
  // Pins of 5 and 32 bits meet at ReadReg1
  // Pins of 5 and 32 bits meet at ReadReg2
  // Pins of 5 and 32 bits meet at ReadData1
  // Pins of 5 and 32 bits meet at ReadData2
endmodule

/* Test case Register File Test:
WriteReg WriteData RegWrite Clock ReadReg1 ReadReg2 ReadData1 ReadData2

# $1 = 25
1 25 1 C 1 0 25 0

# $2 = 30
2 30 1 C 0 2 0 30

# $(N+1) = (N+1)
loop(N, 30)
	(N+1) (N+1) 1 C (N+1) (N) (N+1) (N)
end loop

# $(N+1) = N-60
loop(N, 30)
	(N+1) (N-60) 1 C (N+1) (N+1) (N-60) (N-60)
end loop

# Try writing to $0. This should not write anything
0 25 1 C 0 0 0 0

# try writing when RegWrite = 0
# (the registers should still have their old values)
loop(N, 30)
	(N+1) (N+80) 0 C (N+1) (N+1) (N-60) (N-60)
end loop
*/
